// Logisim project Proiect FD.circ as structural Verilog: 1 circuit, main circuit main
module main (
  input  A,
  input  B,
  input  C,
  input  D,
  input  E,
  output out_6
);

  wire and_1_out, nand_1_out, nor_1_out;

  nor nor_1 (nor_1_out, A, B);
  and and_1 (and_1_out, C, D, E);
  nand nand_1 (nand_1_out, A, nor_1_out, C);
  nor nor_2 (out_6, nand_1_out, and_1_out);

  // Notes on the sheet:
  //   F
  //   G
  //   H
  //   I
  //   J
  //   K
  //   L
endmodule
